// Logisim project exp3_jk_and_d_flip_flop.circ as structural Verilog: 1 circuit, main circuit main
module main (
  input  J,
  input  K,
  input  D,
  input  CLR_JK__Async,
  input  CLR_D__Async,
  input  GATE_J,
  input  GATE_D,
  input  GATE_K,
  input  GATE_CLR_JK,
  output Q_JK,
  output Q_D,
  output nQ_JK,
  output nQ_D,
  output GATE_Q_JK,
  output GATE_Q_D,
  output GATE_nQ_JK,
  output GATE_nQ_D
);

  wire CLK_D_out, CLK_JK_out, GATE_CLK_D_out, GATE_CLK_JK_out, nand_1_out, nand_2_out, nand_3_out,
       nand_4_out, nand_5_out, nand_6_out, nand_9_out, nand_10_out, not_1_out, not_2_out, not_3_out;

  Clock GATE_CLK_JK (.out(GATE_CLK_JK_out));
  Clock CLK_JK (.out(CLK_JK_out));
  not not_1 (not_1_out, GATE_CLR_JK);
  nand nand_1 (nand_1_out, GATE_nQ_JK, GATE_J, GATE_CLK_JK_out);
  nand nand_2 (nand_2_out, GATE_CLK_JK_out, GATE_K, GATE_Q_JK);
  J_K_Flip_Flop #(.trigger("falling")) JK_FF (
    .J(J), .clk(CLK_JK_out), .K(K), .Q(Q_JK), .Qn(nQ_JK), .reset(CLR_JK__Async));  // open: preset, en
  nand nand_3 (nand_3_out, nand_1_out, nand_4_out);
  not not_2 (not_2_out, GATE_CLK_JK_out);
  nand nand_4 (nand_4_out, nand_3_out, nand_2_out, not_1_out);
  nand nand_5 (nand_5_out, nand_3_out, not_2_out);
  nand nand_6 (nand_6_out, not_2_out, nand_4_out);
  nand nand_7 (GATE_Q_JK, nand_5_out, GATE_nQ_JK);
  nand nand_8 (GATE_nQ_JK, GATE_Q_JK, nand_6_out, not_1_out);
  Clock CLK_D (.out(CLK_D_out));
  Clock GATE_CLK_D (.out(GATE_CLK_D_out));
  not not_3 (not_3_out, GATE_D);
  D_Flip_Flop #(.trigger("falling")) D_FF (
    .clk(CLK_D_out), .D(D), .Q(Q_D), .Qn(nQ_D), .reset(CLR_D__Async));  // open: preset, en
  nand nand_9 (nand_9_out, GATE_D, GATE_CLK_D_out);
  nand nand_10 (nand_10_out, GATE_CLK_D_out, not_3_out);
  nand nand_11 (GATE_Q_D, nand_9_out, GATE_nQ_D);
  nand nand_12 (GATE_nQ_D, GATE_Q_D, nand_10_out);

  // Notes on the sheet:
  //   PART A: JK FLIP-FLOP (INTEGRATED COMPONENT)
  //   JK TRUTH TABLE:
  //   J=0, K=0 -> Hold | J=0, K=1 -> Reset (0)
  //   J=1, K=0 -> Set (1) | J=1, K=1 -> Toggle (~Q)
  //   CLR=1   -> Q = 0 (Asynchronous Override)
  //   PART C: GATE-LEVEL MASTER-SLAVE J-K FLIP-FLOP (NAND GATES)
  //   Master Stage (Active High CLK) + Slave Stage (Active Low CLK) - Free of Race Conditions
  //   EXPERIMENT 3: VERIFICATION OF JK AND D FLIP-FLOPS
  //   Top: Integrated Library Components | Bottom: Gate-Level (NAND Gates) Implementations
  //   PART B: D FLIP-FLOP (INTEGRATED COMPONENT)
  //   D TRUTH TABLE:
  //   CLK v, D=0 -> Q=0 | CLK v, D=1 -> Q=1
  //   No Clock   -> Q(t+1) = Q(t) (Hold)
  //   CLR=1      -> Q = 0 (Asynchronous Override)
  //   PART D: GATE-LEVEL CLOCKED D LATCH / FLIP-FLOP (NAND GATES)
  //   4 NAND Gates + Inverter: When CLK=1 Q follows D, When CLK=0 Q holds state
endmodule
